// Logisim project Projeto_versao4.0.circ as structural Verilog: 1 circuit, main circuit main
module main (
  input  in_1,
  input  [7:0] in_2,
  output [7:0] out_3
);

  wire clock_1_out, comparator_1_lt, comparator_2_eq, comparator_3_eq, comparator_4_eq, comparator_5_eq,
       undriven;
  wire [1:1] rom_1_data_2;
  wire [6:0] multiplexer_1_out, rom_1_data;
  wire [7:0] adder_1_out, adder_2_out, adder_3_out, bit_extender_1_out, bit_extender_2_out,
       multiplexer_2_out, multiplexer_3_out, multiplexer_4_out, multiplexer_5_out, multiplexer_6_out,
       multiplexer_7_out, not_1_out, register_1_q, subtractor_1_out;

  Clock clock_1 (.out(clock_1_out));
  Adder adder_1 (.a(in_2), .b(register_1_q), .out(adder_1_out), .cin(in_1));  // open: cout
  Register register_1 (.D(adder_1_out), .en(undriven), .clk(clock_1_out), .Q(register_1_q));  // open: clr
  ROM rom_1 (.addr(register_1_q), .data({rom_1_data_2[1], rom_1_data}));
  assign not_1_out = ~out_3;  // NOT_Gate not_1, 8 bits wide
  Comparator comparator_1 (.a(out_3), .b({8{1'b0}}), .lt(comparator_1_lt));  // open: gt, eq
  Adder adder_2 (.a(not_1_out), .b(8'h1), .out(adder_2_out));  // open: cin, cout
  Comparator #(.width(3)) comparator_2 (
    .a(3'b100), .b({rom_1_data_2[1], rom_1_data[6:5]}), .eq(comparator_2_eq));  // open: gt, lt
  Comparator #(.width(1)) comparator_3 (.a(rom_1_data_2[1]), .b(1'b0), .eq(comparator_3_eq));  // open: gt, lt
  Comparator #(.width(2)) comparator_4 (
    .a({rom_1_data_2[1], rom_1_data[6]}), .b(2'b11), .eq(comparator_4_eq));  // open: gt, lt
  Comparator comparator_5 (.a({rom_1_data_2[1], rom_1_data}), .b(8'hc0), .eq(comparator_5_eq));  // open: gt, lt
  assign bit_extender_1_out = {{3{1'b0}}, rom_1_data[4:0]};  // Bit_Extender bit_extender_1
  assign bit_extender_2_out = {{1{multiplexer_1_out[6]}}, multiplexer_1_out};  // Bit_Extender bit_extender_2
  Multiplexer #(.width(7)) multiplexer_1 (
    .in1(rom_1_data), .out(multiplexer_1_out), .sel(comparator_3_eq));  // open: in0
  Adder adder_3 (.a(out_3), .b(bit_extender_1_out), .out(adder_3_out));  // open: cin, cout
  Subtractor subtractor_1 (.a(out_3), .b(bit_extender_1_out), .out(subtractor_1_out));  // open: bin, bout
  Multiplexer #(.width(8)) multiplexer_2 (
    .in0(multiplexer_4_out), .in1(multiplexer_3_out), .out(multiplexer_2_out), .sel(comparator_5_eq));
  Multiplexer #(.width(8)) multiplexer_3 (
    .in0(out_3), .in1(adder_2_out), .out(multiplexer_3_out), .sel(comparator_1_lt));
  Multiplexer #(.width(8)) multiplexer_4 (.in0(out_3), .in1({8{1'b0}}), .out(multiplexer_4_out), .sel(comparator_1_lt));
  Multiplexer #(.width(8)) multiplexer_5 (
    .in0(subtractor_1_out), .in1(adder_3_out), .out(multiplexer_5_out), .sel(comparator_2_eq));
  Multiplexer #(.width(8)) multiplexer_6 (
    .in0(multiplexer_5_out), .in1(bit_extender_2_out), .out(multiplexer_6_out), .sel(comparator_3_eq));
  Multiplexer #(.width(8)) multiplexer_7 (
    .in0(multiplexer_6_out), .in1(multiplexer_2_out), .out(multiplexer_7_out), .sel(comparator_4_eq));
  Register R1 (.D(multiplexer_7_out), .en(undriven), .clk(clock_1_out), .Q(out_3));  // open: clr

  // Notes on the sheet:
  //   contents of rom_1 (hex, n*v repeats v):
  //   21 82 be c0 aa c0 b4 c1 82 80 80
  //   abs
  //   addi/subi
  //   li
  //   compara com 0
  //   simétrico
  //   relu
  //   li (1)
  //   abs/relu- 1
  //   li/subi/addi- 0
  //   abs ou relu (4)
  //   addi ou subi (3)
  //   li ou addi/subi (2)
  //   MSF (5)
endmodule
